# Fritzing sketch sketch_light (saved by Fritzing 0.9.3b)
breadboards: 1

parts:
  Onderdeel1 = Arduino Uno (Rev3) - ICSP
  R1 = Photocell (LDR) [package=THT]
  R2 = Resistor [tolerance=±5% resistance=680 package="0603 [SMD]"]

nets:
  N1: Onderdeel1.A0, R1.pin_0, R2.Pin_0
  N2: Onderdeel1.5V, R1.pin_1
  N3: Onderdeel1.GND, R2.Pin_1
