# Fritzing sketch sketch_temp (saved by Fritzing 0.9.3b)
breadboards: 1

parts:
  Onderdeel1 = Arduino Uno (Rev3) - ICSP
  T1 = TMP36 Temperature Sensor [package="TO92 [THT]"]

nets:
  N1: Onderdeel1.A1, T1.Vout
  N2: Onderdeel1.5V, T1.+Vs
  GND: Onderdeel1.GND, T1.GND
